// Logisim project generateKeyStream.circ as structural Verilog: 6 circuits, main circuit main
module main (
  input  [7:0] data,
  input  data_av,
  output Done,
  output [3:0] Current_State
);

  wire clk_out, generate_keystream_1_ld, generate_keystream_1_sel, not_1_out, rst_out;
  wire [7:0] controlled_buffer_1_out, generate_keystream_1_addr, generate_keystream_1_data_out, reg_mem_q;

  // Probe on data
  Clock clk (.out(clk_out));
  Button rst (.out(rst_out));
  Generate_KeyStream generate_keystream_1 (
    .data_in(reg_mem_q), .data(data), .data_av(data_av), .clk(clk_out), .rst(rst_out),
    .addr(generate_keystream_1_addr), .data_out(generate_keystream_1_data_out),
    .sel(generate_keystream_1_sel), .ld(generate_keystream_1_ld), .done(Done), .Current_State(Current_State));
  assign controlled_buffer_1_out = not_1_out ? generate_keystream_1_data_out : 8'bz;  // Controlled_Buffer controlled_buffer_1
  not not_1 (not_1_out, generate_keystream_1_ld);
  // Probe on Current_State
  RAM ram_1 (
    .addr(generate_keystream_1_addr), .data(controlled_buffer_1_out), .sel(generate_keystream_1_sel),
    .clk(clk_out), .ld(generate_keystream_1_ld), .clr(rst_out));
  Register reg_mem (
    .D(controlled_buffer_1_out), .en(generate_keystream_1_sel), .Q(reg_mem_q), .clk(clk_out), .clr(rst_out));
endmodule

// Data Path
module DataPath (
  input  [7:0] data_in,
  input  wrState,
  input  wrI,
  input  selSum2,
  input  selSum3,
  input  wrStateSize,
  input  [7:0] data,
  input  wrJ,
  input  wrTextSize,
  input  selSum0,
  input  selSum1,
  input  wrT,
  input  wrKeyStream,
  input  selT,
  input  wrK,
  input  clk,
  input  rst,
  input  clearAux,
  output [7:0] addr,
  output [7:0] data_out,
  output k_lt_textSize
);

  wire or_1_out;
  wire [6:0] subtractor_1_out;
  wire [7:0] divider_1_rem, multiplexer_1_out, multiplexer_2_out, multiplexer_3_out, reg_i_q, reg_j_q,
       reg_k_q, reg_keyStream_q, reg_state_q, reg_stateSize_q, reg_t_q, reg_textSize_q;

  Register reg_state (.D(data), .en(wrState), .Q(reg_state_q), .clk(clk), .clr(rst));
  Register reg_stateSize (.D(data), .en(wrStateSize), .Q(reg_stateSize_q), .clk(clk), .clr(rst));
  Register reg_textSize (.D(data), .en(wrTextSize), .Q(reg_textSize_q), .clk(clk), .clr(rst));
  Register reg_keyStream (.D(data), .en(wrKeyStream), .Q(reg_keyStream_q), .clk(clk), .clr(rst));
  or or_1 (or_1_out, rst, clearAux);
  Multiplexer #(.width(8), .enable("false")) multiplexer_1 (
    .in0(divider_1_rem), .in1(data_in), .out(multiplexer_1_out), .sel(selT));
  Register reg_i (.D(divider_1_rem), .en(wrI), .Q(reg_i_q), .clk(clk), .clr(or_1_out));
  Register reg_j (.D(divider_1_rem), .en(wrJ), .Q(reg_j_q), .clk(clk), .clr(or_1_out));
  Register reg_t (.D(multiplexer_1_out), .en(wrT), .Q(reg_t_q), .clk(clk), .clr(or_1_out));
  Multiplexer #(.select(2), .width(8), .enable("false")) multiplexer_2 (
    .in0(8'h1), .in1(data_in), .in2(reg_state_q), .in3(reg_keyStream_q), .out(multiplexer_2_out),
    .sel({selSum3, selSum2}));
  Multiplexer #(.select(2), .width(8), .enable("false")) multiplexer_3 (
    .in0(reg_i_q), .in1(reg_j_q), .in2(reg_t_q), .in3(reg_k_q), .out(multiplexer_3_out),
    .sel({selSum1, selSum0}));
  Adder adder_1 (.a(multiplexer_2_out), .b(multiplexer_3_out), .out(addr));  // open: cin, cout
  Divider divider_1 (.a(addr), .b(reg_stateSize_q), .rem(divider_1_rem));  // open: out, upper
  Register reg_k (.D(addr), .en(wrK), .Q(reg_k_q), .clk(clk), .clr(or_1_out));
  Multiplexer #(.width(8), .enable("false")) multiplexer_4 (.in0(data_in), .in1(reg_t_q), .out(data_out), .sel(selT));
  Subtractor subtractor_1 (
    .a(reg_k_q), .b(reg_textSize_q), .out({k_lt_textSize, subtractor_1_out}));  // open: bin, bout
endmodule

module NextState (
  input  Q3,
  input  Q2,
  input  Q1,
  input  Q0,
  input  data_av,
  input  k_lt_textSize,
  output D3,
  output D2,
  output D1,
  output D0
);

  wire and_1_out, and_2_out, and_3_out, and_4_out, and_5_out, and_6_out, and_7_out, and_8_out, and_9_out,
       and_10_out, and_11_out, and_12_out, and_13_out, and_14_out, and_15_out, and_16_out, and_17_out,
       and_18_out, and_19_out, and_20_out, and_21_out, and_22_out, not_1_out, not_2_out, not_3_out,
       not_4_out, not_5_out, not_6_out, not_7_out, not_8_out, not_9_out, not_10_out, not_11_out, not_12_out,
       not_13_out, not_14_out, not_15_out, not_16_out, not_17_out, not_18_out, not_19_out, not_20_out,
       not_21_out, not_22_out, not_23_out, not_24_out, not_25_out, not_26_out, not_27_out, not_28_out,
       not_29_out;

  not not_1 (not_1_out, Q2);
  not not_2 (not_2_out, Q1);
  not not_3 (not_3_out, Q2);
  not not_4 (not_4_out, Q1);
  not not_5 (not_5_out, Q1);
  not not_6 (not_6_out, Q0);
  not not_7 (not_7_out, Q1);
  not not_8 (not_8_out, Q3);
  not not_9 (not_9_out, Q2);
  not not_10 (not_10_out, data_av);
  not not_11 (not_11_out, Q3);
  not not_12 (not_12_out, Q0);
  not not_13 (not_13_out, Q2);
  not not_14 (not_14_out, Q0);
  not not_15 (not_15_out, Q1);
  not not_16 (not_16_out, Q1);
  not not_17 (not_17_out, Q2);
  not not_18 (not_18_out, Q0);
  not not_19 (not_19_out, Q3);
  not not_20 (not_20_out, Q2);
  not not_21 (not_21_out, data_av);
  not not_22 (not_22_out, Q1);
  not not_23 (not_23_out, Q0);
  not not_24 (not_24_out, Q3);
  not not_25 (not_25_out, Q0);
  not not_26 (not_26_out, Q2);
  not not_27 (not_27_out, Q0);
  not not_28 (not_28_out, Q1);
  not not_29 (not_29_out, Q0);
  and and_1 (and_1_out, Q2, Q1, Q0);
  and and_2 (and_2_out, Q3, not_1_out);
  and and_3 (and_3_out, Q3, not_2_out);
  and and_4 (and_4_out, not_3_out, Q1, Q0, data_av);
  and and_5 (and_5_out, Q2, not_4_out, k_lt_textSize);
  and and_6 (and_6_out, Q2, not_5_out, Q0);
  and and_7 (and_7_out, Q2, Q1, not_6_out);
  and and_8 (and_8_out, Q3, Q1, Q0);
  and and_9 (and_9_out, Q3, Q2);
  and and_10 (and_10_out, not_7_out, Q0, data_av);
  and and_11 (and_11_out, not_8_out, not_9_out, Q1, not_10_out);
  and and_12 (and_12_out, not_11_out, Q1, not_12_out);
  and and_13 (and_13_out, not_13_out, Q1, not_14_out);
  and and_14 (and_14_out, Q2, not_15_out, Q0);
  and and_15 (and_15_out, Q3, not_16_out, Q0);
  and and_16 (and_16_out, not_17_out, not_18_out, data_av);
  and and_17 (and_17_out, not_19_out, not_20_out, Q0, not_21_out);
  and and_18 (and_18_out, Q2, not_22_out, not_23_out, k_lt_textSize);
  and and_19 (and_19_out, not_24_out, Q2, Q1, not_25_out);
  and and_20 (and_20_out, Q3, not_26_out, not_27_out);
  and and_21 (and_21_out, Q3, not_28_out, not_29_out);
  and and_22 (and_22_out, Q3, Q2, Q1, Q0);
  or or_1 (D3, and_1_out, and_2_out, and_3_out);
  or or_2 (D2, and_4_out, and_5_out, and_6_out, and_7_out, and_8_out, and_9_out);
  or or_3 (D1, and_10_out, and_11_out, and_12_out, and_13_out, and_14_out, and_15_out);
  or or_4 (D0, and_16_out, and_17_out, and_18_out, and_19_out, and_20_out, and_21_out, and_22_out);
endmodule

module Output (
  input  Q3,
  input  Q2,
  input  Q1,
  input  Q0,
  input  k_lt_textSize,
  output wrI,
  output wrJ,
  output wrK,
  output wrT,
  output selT,
  output selSum0,
  output selSum1,
  output selSum2,
  output wrState,
  output selSum3,
  output wrStateSize,
  output clearAux,
  output wrTextSize,
  output wrKeyStream,
  output sel,
  output done,
  output ld
);

  wire and_1_out, and_2_out, and_3_out, and_4_out, and_5_out, and_6_out, and_7_out, and_9_out, and_10_out,
       and_11_out, and_15_out, and_16_out, and_17_out, and_18_out, and_19_out, and_20_out, and_21_out,
       and_22_out, and_23_out, and_24_out, and_25_out, and_26_out, and_27_out, not_1_out, not_2_out,
       not_3_out, not_4_out, not_5_out, not_6_out, not_7_out, not_8_out, not_9_out, not_10_out, not_11_out,
       not_12_out, not_13_out, not_14_out, not_15_out, not_16_out, not_17_out, not_18_out, not_19_out,
       not_20_out, not_21_out, not_22_out, not_23_out, not_24_out, not_25_out, not_26_out, not_27_out,
       not_28_out, not_29_out, not_30_out, not_31_out, not_32_out, not_33_out, not_34_out, not_35_out,
       not_36_out, not_37_out, not_38_out, not_39_out, not_40_out, not_41_out, not_42_out, not_43_out,
       not_44_out, not_45_out, not_46_out, not_47_out, not_48_out, not_49_out, not_50_out, not_51_out,
       not_52_out, not_53_out, not_54_out, not_55_out, not_56_out, not_57_out;

  not not_1 (not_1_out, Q3);
  not not_2 (not_2_out, Q0);
  not not_3 (not_3_out, Q1);
  not not_4 (not_4_out, Q3);
  not not_5 (not_5_out, Q0);
  not not_6 (not_6_out, Q0);
  not not_7 (not_7_out, Q3);
  not not_8 (not_8_out, Q0);
  not not_9 (not_9_out, Q2);
  not not_10 (not_10_out, Q3);
  not not_11 (not_11_out, Q0);
  not not_12 (not_12_out, Q2);
  not not_13 (not_13_out, Q1);
  not not_14 (not_14_out, Q3);
  not not_15 (not_15_out, Q2);
  and and_1 (and_1_out, not_14_out, not_15_out, not_16_out);
  not not_16 (not_16_out, Q0);
  not not_17 (not_17_out, Q3);
  and and_2 (and_2_out, not_17_out, Q2, Q1);
  and and_3 (and_3_out, Q2, Q1, not_18_out);
  not not_18 (not_18_out, Q0);
  and and_4 (and_4_out, Q3, not_19_out, Q0);
  not not_19 (not_19_out, Q1);
  not not_20 (not_20_out, Q2);
  not not_21 (not_21_out, Q1);
  not not_22 (not_22_out, Q0);
  not not_23 (not_23_out, Q3);
  not not_24 (not_24_out, Q0);
  not not_25 (not_25_out, Q2);
  not not_26 (not_26_out, Q1);
  not not_27 (not_27_out, Q2);
  and and_5 (and_5_out, not_27_out, Q1, not_28_out);
  not not_28 (not_28_out, Q0);
  not not_29 (not_29_out, Q3);
  and and_6 (and_6_out, not_29_out, Q2, Q0);
  and and_7 (and_7_out, Q3, not_30_out);
  not not_30 (not_30_out, Q1);
  not not_31 (not_31_out, Q3);
  and and_8 (clearAux, not_31_out, not_32_out);
  not not_32 (not_32_out, Q2);
  not not_33 (not_33_out, Q3);
  and and_9 (and_9_out, not_33_out, Q2, Q0);
  and and_10 (and_10_out, Q3, not_34_out, not_35_out);
  not not_34 (not_34_out, Q2);
  not not_35 (not_35_out, Q0);
  and and_11 (and_11_out, Q3, not_36_out);
  not not_36 (not_36_out, Q1);
  not not_37 (not_37_out, Q3);
  not not_38 (not_38_out, Q2);
  not not_39 (not_39_out, Q0);
  not not_40 (not_40_out, Q1);
  not not_41 (not_41_out, Q0);
  and and_12 (wrI, not_1_out, Q2, k_lt_textSize, not_2_out, not_3_out);
  and and_13 (wrJ, not_4_out, Q2, Q1, not_5_out);
  and and_14 (wrK, Q3, Q2, Q1, not_6_out);
  and and_15 (and_15_out, not_7_out, Q2, Q1, not_8_out);
  or or_1 (wrT, and_15_out, and_16_out);
  and and_16 (and_16_out, Q3, not_9_out, Q1, Q0);
  and and_17 (and_17_out, not_10_out, Q1, not_11_out);
  or or_2 (selT, and_17_out, and_18_out);
  and and_18 (and_18_out, Q3, not_12_out, not_13_out, Q0);
  or or_3 (selSum0, and_1_out, and_2_out, and_3_out, and_4_out);
  and and_19 (and_19_out, Q3, not_20_out, Q1, Q0);
  or or_4 (selSum1, and_19_out, and_20_out, and_21_out);
  and and_20 (and_20_out, Q3, Q2, not_21_out);
  and and_21 (and_21_out, Q3, Q2, not_22_out);
  and and_22 (and_22_out, not_23_out, Q2, Q1, not_24_out);
  or or_5 (selSum2, and_22_out, and_23_out, and_24_out);
  and and_23 (and_23_out, Q3, not_25_out, Q1, Q0);
  and and_24 (and_24_out, Q3, Q2, not_26_out, Q0);
  or or_6 (selSum3, and_5_out, and_6_out, and_7_out);
  or or_7 (sel, and_9_out, and_10_out, and_11_out);
  and and_25 (and_25_out, not_37_out, Q2, Q0);
  and and_26 (and_26_out, Q3, not_38_out, Q1, not_39_out);
  or or_8 (ld, and_25_out, and_26_out, and_27_out);
  and and_27 (and_27_out, Q3, Q2, not_40_out, not_41_out);
  not not_42 (not_42_out, Q3);
  not not_43 (not_43_out, Q2);
  not not_44 (not_44_out, Q1);
  not not_45 (not_45_out, Q0);
  not not_46 (not_46_out, Q1);
  not not_47 (not_47_out, Q2);
  not not_48 (not_48_out, Q3);
  not not_49 (not_49_out, Q0);
  not not_50 (not_50_out, Q2);
  not not_51 (not_51_out, Q3);
  not not_52 (not_52_out, Q2);
  not not_53 (not_53_out, Q3);
  and and_28 (wrState, not_42_out, not_43_out, not_44_out, not_45_out);
  and and_29 (wrStateSize, Q0, not_46_out, not_47_out, not_48_out);
  and and_30 (wrTextSize, not_49_out, Q1, not_50_out, not_51_out);
  and and_31 (wrKeyStream, Q0, Q1, not_52_out, not_53_out);
  not not_54 (not_54_out, Q0);
  not not_55 (not_55_out, Q1);
  not not_56 (not_56_out, Q3);
  not not_57 (not_57_out, k_lt_textSize);
  and and_32 (done, not_54_out, not_55_out, Q2, not_56_out, not_57_out);
endmodule

// Control Path
module ControlPath (
  input  data_av,
  input  k_lt_textSize,
  input  clk,
  input  rst,
  output [3:0] Current_State,
  output wrI,
  output wrJ,
  output wrT,
  output wrK,
  output selT,
  output selSum0,
  output selSum1,
  output selSum2,
  output selSum3,
  output clearAux,
  output sel,
  output wrState,
  output wrStateSize,
  output wrTextSize,
  output ld,
  output wrKeyStream,
  output done
);

  wire [3:0] nextstate_1_d0;

  NextState nextstate_1 (
    .Q3(Current_State[3]), .Q2(Current_State[2]), .Q1(Current_State[1]), .Q0(Current_State[0]),
    .data_av(data_av), .k_lt_textSize(k_lt_textSize), .D3(nextstate_1_d0[3]), .D2(nextstate_1_d0[2]),
    .D1(nextstate_1_d0[1]), .D0(nextstate_1_d0[0]));
  Register #(.width(4)) register_1 (.D(nextstate_1_d0), .Q(Current_State), .clk(clk), .clr(rst));  // open: en
  Output output_1 (
    .Q3(Current_State[3]), .wrI(wrI), .Q2(Current_State[2]), .Q1(Current_State[1]), .wrJ(wrJ),
    .Q0(Current_State[0]), .wrK(wrK), .wrT(wrT), .selT(selT), .selSum0(selSum0), .selSum1(selSum1),
    .selSum2(selSum2), .selSum3(selSum3), .clearAux(clearAux), .sel(sel), .ld(ld), .wrState(wrState),
    .wrStateSize(wrStateSize), .wrTextSize(wrTextSize), .wrKeyStream(wrKeyStream), .done(done),
    .k_lt_textSize(k_lt_textSize));
endmodule

// Generate Key Stream
module Generate_KeyStream (
  input  [7:0] data_in,
  input  [7:0] data,
  input  data_av,
  input  clk,
  input  rst,
  output [7:0] addr,
  output [7:0] data_out,
  output sel,
  output ld,
  output done,
  output [3:0] Current_State
);

  wire controlpath_1_clearaux, controlpath_1_selsum0, controlpath_1_selsum1, controlpath_1_selsum2,
       controlpath_1_selsum3, controlpath_1_selt, controlpath_1_wri, controlpath_1_wrj, controlpath_1_wrk,
       controlpath_1_wrkeystream, controlpath_1_wrstate, controlpath_1_wrstatesize, controlpath_1_wrt,
       controlpath_1_wrtextsize, datapath_1_k_lt_textsize;

  ControlPath controlpath_1 (
    .data_av(data_av), .k_lt_textSize(datapath_1_k_lt_textsize), .clk(clk), .rst(rst),
    .wrI(controlpath_1_wri), .wrJ(controlpath_1_wrj), .wrT(controlpath_1_wrt), .wrK(controlpath_1_wrk),
    .selT(controlpath_1_selt), .selSum0(controlpath_1_selsum0), .selSum1(controlpath_1_selsum1),
    .selSum2(controlpath_1_selsum2), .selSum3(controlpath_1_selsum3), .clearAux(controlpath_1_clearaux),
    .sel(sel), .wrState(controlpath_1_wrstate), .wrStateSize(controlpath_1_wrstatesize),
    .wrTextSize(controlpath_1_wrtextsize), .ld(ld), .wrKeyStream(controlpath_1_wrkeystream), .done(done),
    .Current_State(Current_State));
  DataPath datapath_1 (
    .data_in(data_in), .wrI(controlpath_1_wri), .data(data), .wrJ(controlpath_1_wrj),
    .wrT(controlpath_1_wrt), .wrK(controlpath_1_wrk), .clk(clk), .rst(rst), .addr(addr), .data_out(data_out),
    .k_lt_textSize(datapath_1_k_lt_textsize), .wrState(controlpath_1_wrstate),
    .wrStateSize(controlpath_1_wrstatesize), .wrTextSize(controlpath_1_wrtextsize),
    .wrKeyStream(controlpath_1_wrkeystream), .selT(controlpath_1_selt), .selSum2(controlpath_1_selsum2),
    .selSum0(controlpath_1_selsum0), .selSum3(controlpath_1_selsum3), .selSum1(controlpath_1_selsum1),
    .clearAux(controlpath_1_clearaux));
endmodule
